# Fritzing sketch Esp8266Sim808 (saved by Fritzing 0.9.3b)
circuit board: 7.39662cm x 5.69345cm
perfboards: 1

parts:
  V1 = DC Power [voltage=12V]
  C4 = Ceramic Capacitor [capacitance=100nF voltage=16V package="100 mil [THT, multilayer]"]
  R3 = Resistor [tolerance=±5% resistance=4.7k package=THT]
  BK-808_v2 = Adafruit FONA 808 Breakout [part_number=www.and-global.com]
  C3 = Ceramic Capacitor [capacitance=100nF voltage=16V package="100 mil [THT, multilayer]"]
  LM1 = RioRand LM2596
  BME280 = BME280 Breakout
  R1 = Resistor [tolerance=±5% resistance=680k package=THT]
  WeMos_D1_Mini1_lite = WeMos D1 Mini
  R2 = Resistor [tolerance=±5% resistance=100k package=THT]
  C2 = Electrolytic Capacitor [capacitance=1µF voltage=16V package="100 mil [THT, electrolytic]"]
  C1 = Electrolytic Capacitor [capacitance=1µF voltage=16V package="100 mil [THT, electrolytic]"]
  U2 = MCP1703 Voltage Regulator [part_number=SOT-89 package="TO92 [THT]"]

nets:
  N1: V1.V+, LM1.Pin_0, R1.Pin_1, C2.+, U2.Vin
  N2: V1.V-, C3.0, LM1.Pin_1, R2.Pin_0
  N3: C4.0, WeMos_D1_Mini1_lite.G, C2.-, C1.-
  3.3V: C4.1, BME280.3.3V, WeMos_D1_Mini1_lite.3V3
  N4: R3.Pin_0, C1.+
  N5: BK-808_v2.+5V, LM1.Pin_2
  N6: BK-808_v2.GND, LM1.Pin_3
  N7: BK-808_v2.RXD, WeMos_D1_Mini1_lite.D5
  N8: BK-808_v2.TXD, WeMos_D1_Mini1_lite.D6
  N9: C3.1, R1.Pin_0, WeMos_D1_Mini1_lite.A0, R2.Pin_1
  N10: BME280.GND, WeMos_D1_Mini1_lite.D4
  N11: BME280.SDI/SDA, WeMos_D1_Mini1_lite.D2
  N12: BME280.SCK/SCL, WeMos_D1_Mini1_lite.D1
  N13: WeMos_D1_Mini1_lite.D0, WeMos_D1_Mini1_lite.RST

custom parts:
  Adafruit FONA 808 Breakout: Cellular + GPS tracking, all in one? Oh yes! Introducing Adafruit FONA 808 MiniGSM + GPS, an all-in-one cellular phone module with that lets you add location-tracking, voice, text, SMS and data to your project in an adorable little package.
  MCP1703 Voltage Regulator: A MCP1703 Low Dropout Fixed Voltage Regulator (available in 1.2V, 1.5V, 1.8V, 2.5V, 2.8V, 3.0V, 3.3V, 4.0V, 5.0V)
